# Fritzing sketch FlowerPot (saved by Fritzing 1.0.4)
breadboards: 1

parts:
  A1 = Particle - Photon2
  M1 = BMP280
  OLED_I2C1 = OLED 128x64 I2C Monochrome Display
  SENS1 = SoilWatch 10
  Part1 = MQ-131 breakout
  Grove1 = Grove Dust Sensor
  Part2 = 12 NeoPixel Ring [part_number=1643]
  Relay1 = Relay - 6 pins [package="DIP (Dual Inline) [THT]"]
  WATER_PUMP1 = water pump/motor  # not connected

nets:
  VCC: A1.Pin_2, A1.Pin_31, M1.VIN, OLED_I2C1.VDD, SENS1.VCC, Relay1.VCC
  GND: A1.Pin_4, A1.Pin_30, M1.GND, OLED_I2C1.GND, SENS1.OUT, Part1.GND, Grove1.GND, Part2.GND, Relay1.GND
  N1: A1.Pin_5, Part1.AO
  N2: A1.Pin_6, Part1.DO
  N3: A1.Pin_7, SENS1.GND
  N4: A1.Pin_8, Grove1.SIG
  N5: A1.Pin_12, Relay1.IN
  N6: A1.Pin_17, M1.SDA, OLED_I2C1.SDA
  N7: A1.Pin_18, M1.SCL, OLED_I2C1.SCK
  N8: A1.Pin_24, A1.Pin_36, Part2.IN
  VCC_2: A1.Pin_26, Part1.VCC, Grove1.VCC, Part2.VDD, Relay1.ON

custom parts:
  Particle - Photon2: The Photon 2 is a microcontroller and Wi-Fi networking developed by particle. Features: 802.11a/b/g/n Wi-Fi, 2.4 GHz and 5 GHz Integrated PCB antenna Integrated U.FL connector for external antenna Integrated RF switch BLE 5 using same antenna as Wi-Fi Realtek RTL8721DM MCU ARM Cortex M33 CPU, 200 MHz 2048 KB (2 MB) user application maximum size 3072 KB (3 MB) of RAM available to user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
  BMP280: Temperature Humidity Barometric presure Sensor, I2C
  SoilWatch 10: SoilWatch 10 - Capacitive soil moisture sensor
  MQ-131 breakout: SKU: 101282
  Grove Dust Sensor: PPD42 Grove Dust Sensor
  12 NeoPixel Ring: 12 ultra bright smart LED NeoPixels are arranged in a circle with 1.5" (37mm) outer diameter. The rings are 'chainable' - connect the output pin of one to the input pin of another. Use only one microcontroller pin to control as many as you can chain together! Each LED is addressable as the driver chip is inside the LED. Each one has ~18mA constant current drive so the color will be very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
  Relay - 6 pins: A DIP stand-in part for whatever IC you want. With 6 pins on a 900mil dual inline package (DIP) footprint.
  water pump/motor: WATER PUMP BY ARDUBLOCKTR
